// Logisim project Processador-MINIPS.circ as structural Verilog: 4 circuits, main circuit main
module main (
  input  CLEAR
);

  wire CLK_out;
  wire [3:0] controle_1_sinal_de_controle, ram_1_data, ram_1_data_2;
  wire [7:0] adder_1_out, PC_q, regs_1_dr1, regs_1_dr2, ula_1_out_4;

  Clock CLK (.out(CLK_out));
  RAM #(.Select("low")) ram_1 (.addr(PC_q), .data({ram_1_data_2, ram_1_data}), .clk(CLK_out));  // open: sel, ld, clr
  Adder adder_1 (.a(PC_q), .b(8'h1), .out(adder_1_out));  // open: cin, cout
  Controle controle_1 (.opcode(ram_1_data_2), .Sinal_de_controle(controle_1_sinal_de_controle));
  Register #(.Select("low")) PC (.D(adder_1_out), .Q(PC_q), .clk(CLK_out), .clr(CLEAR));  // open: en
  Regs regs_1 (
    .dRW(ula_1_out_4), .rw(controle_1_sinal_de_controle[0]), .RW_2(2'b00), .CLK(CLK_out),
    .R1(ram_1_data[3:2]), .R2(ram_1_data[1:0]), .dR1(regs_1_dr1), .dR2(regs_1_dr2));
  ULA ula_1 (.DA(regs_1_dr1), .DB(regs_1_dr2), .out_4(ula_1_out_4), .Sel(controle_1_sinal_de_controle[3:1]));

  // Notes on the sheet:
  //   r1
  //   r2
endmodule

module ULA (
  input  [7:0] DA,
  input  [7:0] DB,
  input  [2:0] Sel,
  output [7:0] out_4
);

  wire [7:0] adder_1_out, and_1_out, demultiplexer_1_out0, demultiplexer_1_out1, multiplexer_1_out,
       nor_1_out, not_1_out, or_1_out, xor_1_out;

  assign not_1_out = ~DB;  // NOT_Gate not_1, 8 bits wide
  Multiplexer #(.width(8), .enable("false")) multiplexer_1 (
    .in0(DB), .in1(not_1_out), .out(multiplexer_1_out), .sel(Sel[0]));
  assign and_1_out = DA & DB;  // AND_Gate and_1, 8 bits wide
  assign or_1_out = DA | DB;  // OR_Gate or_1, 8 bits wide
  assign nor_1_out = ~(DA | DB);  // NOR_Gate nor_1, 8 bits wide
  assign xor_1_out = DA ^ DB;  // XOR_Gate xor_1, 8 bits wide
  Adder adder_1 (.a(DA), .b(multiplexer_1_out), .out(adder_1_out), .cin(Sel[0]));  // open: cout
  Demultiplexer #(.width(8), .enable("false")) demultiplexer_1 (
    .out0(demultiplexer_1_out0), .out1(demultiplexer_1_out1), .in(adder_1_out), .sel(Sel[0]));
  Multiplexer #(.select(3), .width(8), .enable("false")) multiplexer_2 (
    .in0(demultiplexer_1_out0), .in1(demultiplexer_1_out1), .in2(and_1_out), .in3(or_1_out), .in4(nor_1_out),
    .in5(xor_1_out), .in6({8{1'b0}}), .in7({8{1'b0}}), .out(out_4), .sel(Sel));
endmodule

module Controle (
  input  [3:0] opcode,
  output [3:0] Sinal_de_controle
);

  Multiplexer #(.select(4), .width(4), .enable("false")) multiplexer_1 (
    .in0(4'b0001), .in1(4'b0011), .in2(4'b0101), .out(Sinal_de_controle), .sel(opcode));  // open: in3, in4, in5, in6, in7, in8, in9, in10, in11, in12, in13, in14, in15
endmodule

module Regs (
  input  [7:0] dRW,
  input  rw,
  input  [1:0] RW_2,
  input  CLK,
  input  [1:0] R1,
  input  [1:0] R2,
  output [7:0] dR1,
  output [7:0] dR2
);

  wire demultiplexer_1_out0, demultiplexer_1_out1, demultiplexer_1_out2, demultiplexer_1_out3;
  wire [7:0] A_q, B_q, C_q, D_q;

  Demultiplexer #(.select(2), .enable("false")) demultiplexer_1 (
    .out0(demultiplexer_1_out0), .out1(demultiplexer_1_out1), .out2(demultiplexer_1_out2),
    .out3(demultiplexer_1_out3), .in(rw), .sel(RW_2));
  Register #(.Select("low")) A (.D(dRW), .en(demultiplexer_1_out0), .Q(A_q), .clk(CLK));  // open: clr
  Register #(.Select("low")) B (.D(dRW), .en(demultiplexer_1_out1), .Q(B_q), .clk(CLK));  // open: clr
  Register #(.Select("low")) C (.D(dRW), .en(demultiplexer_1_out2), .Q(C_q), .clk(CLK));  // open: clr
  Register #(.Select("low")) D (.D(dRW), .en(demultiplexer_1_out3), .Q(D_q), .clk(CLK));  // open: clr
  Multiplexer #(.select(2), .width(8), .enable("false")) multiplexer_1 (
    .in0(A_q), .in1(B_q), .in2(C_q), .in3(D_q), .out(dR1), .sel(R1));
  Multiplexer #(.select(2), .width(8), .enable("false")) multiplexer_2 (
    .in0(A_q), .in1(B_q), .in2(C_q), .in3(D_q), .out(dR2), .sel(R2));
endmodule
